// Logisim project 8bit_CPU.circ as structural Verilog: 6 circuits, main circuit main
module main (
);

  wire ALUsrc, Branch, clk, clock_1_out, DisplayWrite, HALT, Jump, kbRead, MemWrite, RegWrite, TargetSrc,
       tick_out, ttySel, ttyWrite;
  wire [1:0] BranchSel;
  wire [2:0] ALUOp, rd, RegDataSrc, rs, rt;
  wire [3:0] Display_digit_0, Display_digit_1, Display_digit_2, Display_digit_3;
  wire [6:0] bit_extender_1_out, keyboard_1_data;
  wire [7:0] ALUOut, imm, KB, MemOut, multiplexer_1_out, multiplexer_2_out, multiplexer_3_out,
       multiplexer_4_out, PC_1, PC_FSM_pc, REG_rs, REG_rt;
  wire [19:0] rom_1_data;

  Clock clock_1 (.out(clock_1_out));
  Button tick (.out(tick_out));
  or or_1 (clk, clock_1_out, tick_out);
  Multiplexer #(.select(3), .width(8)) multiplexer_1 (
    .in0(ALUOut), .in1(imm), .in2(REG_rt), .in3(MemOut), .in4(PC_1), .in5(KB), .out(multiplexer_1_out),
    .sel(RegDataSrc));  // open: in6, in7, en
  Hex_Digit_Display hex_digit_display_1 (.value(Display_digit_2));  // open: dp
  Hex_Digit_Display hex_digit_display_2 (.value(Display_digit_3));  // open: dp
  Display Display (
    .CLK(clk), .Data_Lo(REG_rt), .Data_Hi(REG_rs), .WE(DisplayWrite), .Digit_0(Display_digit_0),
    .Digit_1(Display_digit_1), .Digit_2(Display_digit_2), .Digit_3(Display_digit_3));
  Register_File RegFile (
    .REG_rd(multiplexer_1_out), .rd(rd), .Reg_WE(RegWrite), .rs(rs), .rt(rt), .CLK(clk), .REG_rs(REG_rs),
    .REG_rt(REG_rt));
  Multiplexer #(.width(8)) multiplexer_2 (.in0(REG_rt), .in1(imm), .out(multiplexer_2_out), .sel(ALUsrc));  // open: en
  Hex_Digit_Display hex_digit_display_3 (.value(Display_digit_0));  // open: dp
  Hex_Digit_Display hex_digit_display_4 (.value(Display_digit_1));  // open: dp
  ALU ALU (.A(REG_rs), .B(multiplexer_2_out), .ALU_Op(ALUOp), .ALU_Out(ALUOut));
  LED u_HALT (.in(HALT));
  Multiplexer #(.width(8)) multiplexer_3 (.in0(REG_rs), .in1(imm), .out(multiplexer_3_out), .sel(ttySel));  // open: en
  Multiplexer #(.width(8)) multiplexer_4 (
    .in0(imm), .in1(REG_rs), .out(multiplexer_4_out), .sel(TargetSrc));  // open: en
  Bit_Extender #(.out_width(7)) bit_extender_1 (.in(multiplexer_3_out), .out(bit_extender_1_out));
  TTY tty_1 (.data(bit_extender_1_out), .clk(clk), .we(ttyWrite));  // open: clr
  PC_FSM PC_FSM (
    .Jump(Jump), .Branch(Branch), .HALT(HALT), .clk(clk), .offset(imm), .target(multiplexer_4_out),
    .REG_rs(REG_rs), .REG_rt(REG_rt), .in_9(BranchSel), .PC(PC_FSM_pc), .PC_1(PC_1));
  Keyboard keyboard_1 (.clk(clk), .re(kbRead), .data(keyboard_1_data));  // open: clr, avail
  // Probe on PC_FSM_pc
  assign KB = {{1{1'b0}}, keyboard_1_data};  // Bit_Extender bit_extender_2
  Control control_1 (
    .Instruction(rom_1_data), .HALT(HALT), .DisplayWrite(DisplayWrite), .RegWrite(RegWrite),
    .RegDataSrc(RegDataSrc), .MemWrite(MemWrite), .rs(rs), .rt(rt), .rd(rd), .ALUOp(ALUOp), .ALUSrc(ALUsrc),
    .imm(imm), .Jump(Jump), .Branch(Branch), .TargetSrc(TargetSrc), .BranchSel(BranchSel),
    .ttyWrite(ttyWrite), .kbRead(kbRead), .ttySel(ttySel));
  ROM #(.dataWidth(20)) rom_1 (.addr(PC_FSM_pc), .data(rom_1_data));  // open: sel
  RAM #(.bus("separate")) ram_1 (
    .addr(ALUOut), .din(REG_rt), .data(MemOut), .str(MemWrite), .clk(clk));  // open: sel, ld, clr

  // Notes on the sheet:
  //   contents of rom_1 (hex, n*v repeats v):
  //   88081 4040 880c1 880c2 60e88 b800b 1c09b 60a18 5fc18 b8092 d4100 4040 b8089 d40c0
endmodule

module Display (
  input  CLK,
  input  [7:0] Data_Lo,
  input  [7:0] Data_Hi,
  input  WE,
  output [3:0] Digit_0,
  output [3:0] Digit_1,
  output [3:0] Digit_2,
  output [3:0] Digit_3
);

  Register #(.width(16)) register_1 (
    .D({Data_Hi, Data_Lo}), .en(WE), .Q({Digit_3, Digit_2, Digit_1, Digit_0}), .clk(CLK));  // open: clr
endmodule

module ALU (
  input  [7:0] A,
  input  [7:0] B,
  input  [2:0] ALU_Op,
  output [7:0] ALU_Out
);

  wire [2:0] bit_extender_1_out, bit_extender_2_out;
  wire [7:0] adder_1_out, and_1_out, not_1_out, or_1_out, shifter_1_out, shifter_2_out, subtractor_1_out,
       undriven, xor_1_out;

  Bit_Extender #(.out_width(3)) bit_extender_1 (.in(B), .out(bit_extender_1_out));
  Bit_Extender #(.out_width(3)) bit_extender_2 (.in(B), .out(bit_extender_2_out));
  Adder adder_1 (.a(A), .b(B), .out(adder_1_out));  // open: cin, cout
  Subtractor subtractor_1 (.a(A), .b(B), .out(subtractor_1_out));  // open: bin, bout
  assign and_1_out = A & B & undriven;  // AND_Gate and_1, 8 bits wide
  assign or_1_out = undriven | A | B;  // OR_Gate or_1, 8 bits wide
  assign xor_1_out = A ^ B;  // XOR_Gate xor_1, 8 bits wide
  assign not_1_out = ~B;  // NOT_Gate not_1, 8 bits wide
  Shifter shifter_1 (.in(A), .\dist (bit_extender_1_out), .out(shifter_1_out));
  Shifter #(.shift("lr")) shifter_2 (.in(A), .\dist (bit_extender_2_out), .out(shifter_2_out));
  Multiplexer #(.select(3), .width(8)) multiplexer_1 (
    .in0(adder_1_out), .in1(subtractor_1_out), .in2(and_1_out), .in3(or_1_out), .in4(xor_1_out),
    .in5(not_1_out), .in6(shifter_1_out), .in7(shifter_2_out), .out(ALU_Out), .sel(ALU_Op));  // open: en
endmodule

module Register_File (
  input  [7:0] REG_rd,
  input  [2:0] rd,
  input  Reg_WE,
  input  [2:0] rs,
  input  [2:0] rt,
  input  CLK,
  output [7:0] REG_rs,
  output [7:0] REG_rt
);

  wire demultiplexer_1_out1, demultiplexer_1_out2, demultiplexer_1_out3, demultiplexer_1_out4,
       demultiplexer_1_out5, demultiplexer_1_out6, demultiplexer_1_out7;
  wire [7:0] r1, r2, r3, r4, r5, r6, r7;

  Demultiplexer #(.select(3)) demultiplexer_1 (
    .out1(demultiplexer_1_out1), .out2(demultiplexer_1_out2), .out3(demultiplexer_1_out3),
    .out4(demultiplexer_1_out4), .out5(demultiplexer_1_out5), .out6(demultiplexer_1_out6),
    .out7(demultiplexer_1_out7), .in(Reg_WE), .sel(rd));  // open: out0, en
  Register register_1 (.D(REG_rd), .en(demultiplexer_1_out1), .Q(r1), .clk(CLK));  // open: clr
  Register register_2 (.D(REG_rd), .en(demultiplexer_1_out2), .Q(r2), .clk(CLK));  // open: clr
  Register register_3 (.D(REG_rd), .en(demultiplexer_1_out3), .Q(r3), .clk(CLK));  // open: clr
  Register register_4 (.D(REG_rd), .en(demultiplexer_1_out4), .Q(r4), .clk(CLK));  // open: clr
  Register register_5 (.D(REG_rd), .en(demultiplexer_1_out5), .Q(r5), .clk(CLK));  // open: clr
  Register register_6 (.D(REG_rd), .en(demultiplexer_1_out6), .Q(r6), .clk(CLK));  // open: clr
  Register register_7 (.D(REG_rd), .en(demultiplexer_1_out7), .Q(r7), .clk(CLK));  // open: clr
  Multiplexer #(.select(3), .width(8)) multiplexer_1 (
    .in0({8{1'b0}}), .in1(r1), .in2(r2), .in3(r3), .in4(r4), .in5(r5), .in6(r6), .in7(r7), .out(REG_rs),
    .sel(rs));  // open: en
  Multiplexer #(.select(3), .width(8)) multiplexer_2 (
    .in0({8{1'b0}}), .in1(r1), .in2(r2), .in3(r3), .in4(r4), .in5(r5), .in6(r6), .in7(r7), .out(REG_rt),
    .sel(rt));  // open: en
endmodule

module PC_FSM (
  input  Jump,
  input  Branch,
  input  HALT,
  input  clk,
  input  [7:0] offset,
  input  [7:0] target,
  input  [7:0] REG_rs,
  input  [7:0] REG_rt,
  input  [1:0] in_9,
  output [7:0] PC,
  output [7:0] PC_1
);

  wire BranchCTRL, comparator_1_eq, comparator_1_gt, comparator_1_lt, comparator_2_lt, comparator_3_eq,
       comparator_4_eq, multiplexer_2_out, not_1_out, not_2_p2, or_1_out;
  wire [7:0] multiplexer_1_out, multiplexer_3_out;

  Multiplexer #(.width(8)) multiplexer_1 (
    .in0(8'h1), .in1(offset), .out(multiplexer_1_out), .sel(BranchCTRL));  // open: en
  Comparator comparator_1 (.a(REG_rs), .b(REG_rt), .gt(comparator_1_gt), .eq(comparator_1_eq), .lt(comparator_1_lt));
  Adder adder_1 (.a(PC), .b(multiplexer_1_out), .out(PC_1));  // open: cin, cout
  Comparator comparator_2 (.a(REG_rs), .b(REG_rt), .lt(comparator_2_lt));  // open: gt, eq
  or or_1 (or_1_out, comparator_1_gt, comparator_1_eq, comparator_1_lt);
  Comparator comparator_3 (.a(REG_rs), .b(REG_rt), .eq(comparator_3_eq));  // open: gt, lt
  not not_1 (not_1_out, comparator_4_eq);
  Comparator comparator_4 (.a(REG_rs), .b(REG_rt), .eq(comparator_4_eq));  // open: gt, lt
  Multiplexer #(.select(2)) multiplexer_2 (
    .in0(comparator_2_lt), .in1(or_1_out), .in2(comparator_3_eq), .in3(not_1_out), .out(multiplexer_2_out),
    .sel(in_9));  // open: en
  Multiplexer #(.width(8)) multiplexer_3 (.in0(PC_1), .in1(target), .out(multiplexer_3_out), .sel(Jump));  // open: en
  // NOT_Gate not_2: pin names not known; wires that end beside it: HALT, not_2_p2
  and and_1 (BranchCTRL, multiplexer_2_out, Branch);
  Register u_PC (.D(multiplexer_3_out), .en(not_2_p2), .Q(PC), .clk(clk));  // open: clr

  // Other names for the same wires on the sheet: BranchSel[1:0] = in_9
endmodule

module Control (
  input  [19:0] Instruction,
  output HALT,
  output DisplayWrite,
  output RegWrite,
  output [2:0] RegDataSrc,
  output MemWrite,
  output [2:0] rs,
  output [2:0] rt,
  output [2:0] rd,
  output [2:0] ALUOp,
  output ALUSrc,
  output [7:0] imm,
  output Jump,
  output Branch,
  output TargetSrc,
  output [1:0] BranchSel,
  output ttyWrite,
  output kbRead,
  output ttySel
);

  wire add, adi, \and , ani, beq, bge, blt, bne, in, j, jal, jr, ld, li, mov, \not , \or , or_2_out,
       or_3_out, or_4_out, or_5_out, or_6_out, or_7_out, or_8_out, or_9_out, or_10_out, or_11_out, or_12_out,
       or_13_out, or_14_out, or_15_out, or_24_out, ori, oui, out, put, sbi, shl, shr, sli, sri, st, sub,
       undriven, undriven_2, undriven_3, undriven_4, undriven_5, undriven_6, undriven_7, undriven_8, \xor ,
       xri;
  wire [7:0] bit_extender_1_out, bit_extender_2_out, multiplexer_1_out;

  // Decoder #(.select(5)) decoder_1: pin names not known; wires that end beside it: Instruction[18:14], HALT, put, li, mov, st, ld, add, sub, \and , \or , \xor , \not , shl, shr, adi, sbi, ani, ori, xri, sli, sri, j, blt, bge, beq, bne, jal, jr, out, oui, in
  Priority_Encoder priority_encoder_1 (
    .in0(1'b1), .in1(li), .in2(mov), .in3(ld), .in4(jal), .in5(in), .out(RegDataSrc));  // open: in6, in7, en_in, gs, en_out
  buf or_1 (MemWrite, st);  // OR_Gate
  or or_2 (or_2_out, add, adi);
  buf or_3 (or_3_out, undriven);  // OR_Gate
  or or_4 (or_4_out, undriven, undriven_2);
  or or_5 (or_5_out, undriven_2, undriven_3);
  or or_6 (or_6_out, undriven_3, undriven_4);
  buf or_7 (or_7_out, undriven_4);  // OR_Gate
  or or_8 (or_8_out, shr, sri);
  or or_9 (or_9_out, add, adi);
  buf or_10 (or_10_out, undriven_5);  // OR_Gate
  or or_11 (or_11_out, undriven_5, undriven_6);
  or or_12 (or_12_out, undriven_6, undriven_7);
  or or_13 (or_13_out, undriven_7, undriven_8);
  buf or_14 (or_14_out, undriven_8);  // OR_Gate
  or or_15 (or_15_out, shr, sri);
  or or_16 (RegWrite, in, ld, mov, li, or_2_out, or_3_out, or_5_out, or_6_out, \not , or_7_out, or_8_out, jal);
  buf or_17 (DisplayWrite, put);  // OR_Gate
  or or_18 (ALUSrc, st, ld, adi, sbi, ani, ori, xri, sli, sri);
  Priority_Encoder priority_encoder_2 (
    .in0(or_9_out), .in1(or_10_out), .in2(or_11_out), .in3(or_12_out), .in4(or_13_out), .in5(\not ),
    .in6(or_14_out), .in7(or_15_out), .out(ALUOp));  // open: en_in, gs, en_out
  buf or_19 (TargetSrc, jr);  // OR_Gate
  or or_20 (ttyWrite, out, oui);
  // OR_Gate or_21 has open pins: out=kbRead
  or or_22 (Jump, j, jal, jr);
  or or_23 (Branch, blt, bge, beq, bne);
  Priority_Encoder #(.select(2)) priority_encoder_3 (
    .in0(blt), .in1(bge), .in2(beq), .in3(bne), .out(BranchSel));  // open: gs, en_out, en_in
  Priority_Encoder #(.select(1)) priority_encoder_4 (.in0(out), .in1(oui), .out(ttySel));  // open: gs, en_out, en_in
  assign bit_extender_1_out = {{3{Instruction[13]}}, Instruction[13:9]};  // Bit_Extender bit_extender_1
  Multiplexer #(.width(8)) multiplexer_1 (
    .in0(bit_extender_1_out), .in1(bit_extender_2_out), .out(multiplexer_1_out), .sel(or_24_out));  // open: en
  assign bit_extender_2_out = {{3{1'b0}}, Instruction[13:9]};  // Bit_Extender bit_extender_2
  or or_24 (or_24_out, ld, st);
  Multiplexer #(.width(8)) multiplexer_2 (
    .in0(multiplexer_1_out), .in1(Instruction[13:6]), .out(imm), .sel(Instruction[19]));  // open: en

  assign rd = Instruction[2:0];
  assign rs = Instruction[5:3];
  assign rt = Instruction[8:6];

  // Other names for the same wires on the sheet: hlt = HALT; imm8[7:0] = Instruction[13:6];
  //   imm5[4:0] = Instruction[13:9]; opcode[4:0] = Instruction[18:14]; type = Instruction[19]
endmodule
